# Fritzing sketch kitchen (saved by Fritzing 0.9.3b)
circuit board: 8.46667cm x 5.64444cm
breadboards: 1

parts:
  ESP32_DEVKIT = MH-ET LIVE ESP32 DEVKIT 38 pins
  DFPlayer_Mini = DFPlayer MINI [package="DIP (Dual Inline) [THT]"]
  U1 = LIPO-1000mAh [package=lipo-1000]
  SP1 = SPEAKER [package=pcb_mount_speaker]
  Button_1 = Pushbutton [package="[THT]"]
  Button_2 = Pushbutton [package="[THT]"]
  TP1 = TP4056 [chip_label=TP4056 package="DIP (Dual Inline) [THT]"]

nets:
  N1: ESP32_DEVKIT.GND#58, Button_1.Pin_4, Button_2.Pin_4, TP1.pin6
  5V: ESP32_DEVKIT.5V, DFPlayer_Mini.VCC, DFPlayer_Mini.DAC_L, DFPlayer_Mini.SPK1, DFPlayer_Mini.K2/ADC_KEY, SP1.+, TP1.pin3
  N2: ESP32_DEVKIT.GND#64, DFPlayer_Mini.GND
  N3: ESP32_DEVKIT.IO17, DFPlayer_Mini.RX
  N4: ESP32_DEVKIT.IO16, DFPlayer_Mini.TX
  N5: ESP32_DEVKIT.IO4, Button_1.Pin_1, Button_1.Pin_2
  N6: ESP32_DEVKIT.IO15, Button_2.Pin_1, Button_2.Pin_2
  N7: DFPlayer_Mini.SPK2, SP1.-
  N8: U1.+, TP1.pin4
  N9: U1.-, TP1.pin5

custom parts:
  MH-ET LIVE ESP32 DEVKIT 38 pins: http://mh.nodebb.com/topic/2/mh-et-live-esp32-devkit
  DFPlayer MINI: MP3 module by DFRobot.com for playing Music from an SD-Card. Supports WAV and MP3 files.
  TP4056: A DIP stand-in part for whatever IC you want. With 6 pins on a 300mil dual inline package (DIP) footprint.
