# Fritzing sketch room (saved by Fritzing 0.9.3b)
breadboards: 1

parts:
  ESP32 = MH-ET LIVE ESP32 DEVKIT 38 pins
  DFPlayer_Mini = DFPlayer MINI [package="DIP (Dual Inline) [THT]"]
  SP1 = SPEAKER [package=pcb_mount_speaker]
  TP1 = TP4056 [chip_label=TP4056 package="DIP (Dual Inline) [THT]"]
  BAT1 = Battery Holders [package=lipo-1100mAh]
  S5 = Pushbutton [package="[THT]"]
  S6 = Pushbutton [package="[THT]"]
  S7 = Pushbutton [package="[THT]"]

nets:
  N1: ESP32.GND#58, DFPlayer_Mini.GND, TP1.pin6
  5V: ESP32.5V, DFPlayer_Mini.VCC, TP1.pin3
  N2: ESP32.GND#64, S5.Pin_1, S6.Pin_1, S6.Pin_2, S7.Pin_1, S7.Pin_2
  N3: ESP32.IO22, S7.Pin_4
  N4: ESP32.IO21, S6.Pin_4
  N5: ESP32.IO19, S5.Pin_4
  N6: ESP32.IO17, DFPlayer_Mini.RX
  N7: ESP32.IO16, DFPlayer_Mini.TX
  N8: DFPlayer_Mini.SPK1, SP1.+
  N9: DFPlayer_Mini.SPK2, SP1.-
  N10: TP1.pin4, BAT1.+
  N11: TP1.pin5, BAT1.-

custom parts:
  MH-ET LIVE ESP32 DEVKIT 38 pins: http://mh.nodebb.com/topic/2/mh-et-live-esp32-devkit
  DFPlayer MINI: MP3 module by DFRobot.com for playing Music from an SD-Card. Supports WAV and MP3 files.
  TP4056: A DIP stand-in part for whatever IC you want. With 6 pins on a 300mil dual inline package (DIP) footprint.
